# Fritzing sketch pcb (saved by Fritzing 0.9.2b)
circuit board: 5.16225cm x 2.74338cm
breadboards: 1

parts:
  J1 = female pin header, 3 pins [form="♀ (female)"]
  J4 = Screw terminal - 2 pins [package=THT]
  Part1 = Electron

nets:
  N1: J1.pin1, Part1.D1
  N2: J1.pin2, Part1.D2
  N3: J1.pin3, Part1.D3
  N4: J4.pin1, Part1.GND
  N5: J4.pin2, Part1.D0
  N6: Part1.Li+, Part1.Li-
